# Fritzing sketch ventilador-iot (saved by Fritzing 0.9.4)
breadboards: 1

parts:
  Mod1 = KY-019 5V Relay Module [package="Breakout board"]
  Q1 = Basic FET N-Channel [package="TO220 [THT]"]
  Q2 = Basic FET N-Channel [package="TO220 [THT]"]
  Q3 = Basic FET N-Channel [package="TO220 [THT]"]
  R1 = Resistor [tolerance=±5% resistance=10k package=THT]
  R2 = Resistor [tolerance=±5% resistance=10k package=THT]
  R3 = Resistor [tolerance=±5% resistance=10k package=THT]
  M1 = DOIT Esp32 DevKit v1 (30 pins long, 11 pins width) [part_number=ESP32S-PIN30]

nets:
  N1: Mod1.S, M1.D26
  N2: Mod1.+, M1.VIN
  N3: Mod1.-, Q1.source, Q2.source, Q3.source, R1.Pin_1, R2.Pin_1, R3.Pin_1, M1.GND
  N4: Q1.gate, R1.Pin_0, M1.D21
  N5: Q2.gate, R2.Pin_0, M1.D19
  N6: Q3.gate, R3.Pin_0, M1.D18

notes:
  Here goes the LED Strip
  Here goes the fan connection

custom parts:
  KY-019 5V Relay Module: KY-019 5V Relay module, used to control AC circuits.
  DOIT Esp32 DevKit v1 (30 pins long, 11 pins width): The DOIT Esp32 DevKit v1 is one of the development board created by DOIT to evaluate the ESP-WROOM-32 module. It is based on the ESP32 microcontroller that boasts Wifi, Bluetooth, Ethernet and Low Power support all in a single chip. (vanepp) made breadboard work, adjusted pin numbering and labels and reduced size of schematic and cleaned up pcb. This chip is 30pins long (2 x15) and 11 pins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
